// Logisim project 8 bit_adder.circ as structural Verilog
module _2_bit_adder (
  input  [1:0] A,
  input  [1:0] B,
  input  Cin,
  output [1:0] S,
  output Cout
);

  wire n1_bit_adder_1_cout;

  _1_bit_adder u_1_bit_adder_1 (.A(A[0]), .B(B[0]), .Cin(Cin), .S(S[0]), .Cout(n1_bit_adder_1_cout));
  _1_bit_adder u_1_bit_adder_2 (.A(A[1]), .B(B[1]), .Cin(n1_bit_adder_1_cout), .S(S[1]), .Cout(Cout));
endmodule

module _4_bit_adder (
  input  [3:0] A,
  input  [3:0] B,
  input  Cin,
  output [3:0] S,
  output Cout
);

  wire n2_bit_adder_1_cout;

  _2_bit_adder u_2_bit_adder_1 (.A(A[1:0]), .B(B[1:0]), .Cin(Cin), .Cout(n2_bit_adder_1_cout), .S(S[1:0]));
  _2_bit_adder u_2_bit_adder_2 (.A(A[3:2]), .B(B[3:2]), .Cin(n2_bit_adder_1_cout), .Cout(Cout), .S(S[3:2]));
endmodule

module _8_bit_adder (
  input  [7:0] A,
  input  [7:0] B,
  input  Cin,
  output [7:0] S,
  output Cout
);

  wire n4_bit_adder_1_cout;

  _4_bit_adder u_4_bit_adder_1 (.A(A[3:0]), .B(A[3:0]), .Cin(Cin), .Cout(n4_bit_adder_1_cout), .S(S[3:0]));
  _4_bit_adder u_4_bit_adder_2 (.A(A[7:4]), .B(B[7:4]), .Cin(n4_bit_adder_1_cout), .Cout(Cout), .S(S[7:4]));

  assign B[3:0] = A[3:0];
endmodule

module _1_bit_adder (
  input  A,
  input  B,
  input  Cin,
  output S,
  output Cout
);

  wire and_1_out, and_2_out, and_3_out, and_4_out, and_5_out, and_6_out, and_7_out, not_1_out, not_2_out,
       not_3_out, not_4_out, not_5_out, not_6_out;

  not not_1 (not_1_out, A);
  not not_2 (not_2_out, B);
  not not_3 (not_3_out, A);
  not not_4 (not_4_out, Cin);
  not not_5 (not_5_out, B);
  not not_6 (not_6_out, Cin);
  and and_1 (and_1_out, B, Cin);
  and and_2 (and_2_out, A, Cin);
  and and_3 (and_3_out, A, B);
  and and_4 (and_4_out, not_1_out, not_2_out, Cin);
  and and_5 (and_5_out, not_3_out, B, not_4_out);
  and and_6 (and_6_out, A, not_5_out, not_6_out);
  and and_7 (and_7_out, A, B, Cin);
  or or_1 (Cout, and_1_out, and_2_out, and_3_out);
  or or_2 (S, and_4_out, and_5_out, and_6_out, and_7_out);
endmodule
