// Logisim project P3Complex.circ as structural Verilog: 9 circuits, main circuit main
module main (
  input  Reset
);

  wire alu_1_zero, and_1_out, Clk_out, controller_1_alusrca, controller_1_branch, controller_1_memread,
       controller_1_memwrite, controller_1_outsel, controller_1_writeen, ExtOp;
  wire [1:0] ALUSrcB, controller_1_cmpsel, controller_1_jump, controller_1_resulttoreg,
       controller_1_writeregdist;
  wire [2:0] controller_1_aluop;
  wire [4:0] multiplexer_1_out;
  wire [25:0] Jimm;
  wire [31:0] adder_2_out, alu_1_out, bit_extender_1_out, bit_extender_3_out, datamemory_1_out, grf_1_rdata1,
       grf_1_rdata2, ifu_1_pc_current, multiplexer_2_out, multiplexer_3_out, multiplexer_4_out,
       multiplexer_5_out, multiplexer_7_out, PC_4, PC_NEXT, shifter_1_out, sign_ext;
  wire [31:26] ifu_1_instruction;

  Clock Clk (.out(Clk_out));
  // Probe on Jimm[5:0]
  IFU ifu_1 (
    .PC_Update(PC_NEXT), .Reset(Reset), .Instruction({ifu_1_instruction, Jimm}),
    .PC_current(ifu_1_pc_current), .Clk(Clk_out));
  Adder #(.width(32)) adder_1 (.a(32'h4), .b(ifu_1_pc_current), .out(PC_4));  // open: cin, cout
  assign bit_extender_1_out = {{27{1'b0}}, Jimm[10:6]};  // Bit_Extender bit_extender_1
  Shifter #(.width(32)) shifter_1 (.in(sign_ext), .\dist (5'b00010), .out(shifter_1_out));
  assign sign_ext = {{16{Jimm[15]}}, Jimm[15:0]};  // Bit_Extender bit_extender_2
  Controller controller_1 (
    .Op(ifu_1_instruction), .Func(Jimm[5:0]), .MemRead(controller_1_memread),
    .MemWrite(controller_1_memwrite), .WriteEn(controller_1_writeen), .Jump(controller_1_jump),
    .Branch(controller_1_branch), .WriteRegDist(controller_1_writeregdist),
    .ResultToReg(controller_1_resulttoreg), .ALUSrcA(controller_1_alusrca), .ALUSrcB(ALUSrcB),
    .ALUOp(controller_1_aluop), .CmpSel(controller_1_cmpsel), .OutSel(controller_1_outsel), .ExtOp(ExtOp));
  Multiplexer #(.select(2), .width(5), .enable("false")) multiplexer_1 (
    .in0(Jimm[20:16]), .in1(Jimm[15:11]), .in2({5{1'b1}}), .out(multiplexer_1_out),
    .sel(controller_1_writeregdist));  // open: in3
  assign bit_extender_3_out = {{16{1'b0}}, Jimm[15:0]};  // Bit_Extender bit_extender_3
  Multiplexer #(.width(32), .enable("false")) multiplexer_2 (
    .in0(sign_ext), .in1(bit_extender_3_out), .out(multiplexer_2_out), .sel(ExtOp));
  Multiplexer #(.width(32), .enable("false")) multiplexer_3 (
    .in0(PC_4), .in1(adder_2_out), .out(multiplexer_3_out), .sel(and_1_out));
  Adder #(.width(32)) adder_2 (.a(PC_4), .b(shifter_1_out), .out(adder_2_out));  // open: cin, cout
  GRF grf_1 (
    .ReadReg1(Jimm[25:21]), .WriteReg(multiplexer_1_out), .WriteEn(controller_1_writeen),
    .WData(multiplexer_7_out), .RData1(grf_1_rdata1), .RData2(grf_1_rdata2), .ReadReg2(Jimm[20:16]),
    .reset(Reset), .Clk(Clk_out));
  and and_1 (and_1_out, controller_1_branch, alu_1_zero);
  Multiplexer #(.width(32), .enable("false")) multiplexer_4 (
    .in0(grf_1_rdata1), .in1(grf_1_rdata2), .out(multiplexer_4_out), .sel(controller_1_alusrca));
  // Probe on nothing
  Multiplexer #(.select(2), .width(32), .enable("false")) multiplexer_5 (
    .in0(grf_1_rdata2), .in1(multiplexer_2_out), .in2(bit_extender_1_out), .in3({32{1'b0}}),
    .out(multiplexer_5_out), .sel(ALUSrcB));
  Multiplexer #(.select(2), .width(32), .enable("false")) multiplexer_6 (
    .in0(multiplexer_3_out), .in1({ifu_1_pc_current[31:28], Jimm, 2'b00}), .in2(grf_1_rdata1), .out(PC_NEXT),
    .sel(controller_1_jump));  // open: in3
  ALU alu_1 (
    .A(multiplexer_4_out), .B(multiplexer_5_out), .Out(alu_1_out), .ALUOp(controller_1_aluop),
    .CmpSel(controller_1_cmpsel), .Zero(alu_1_zero), .OutSel(controller_1_outsel));
  DataMemory datamemory_1 (
    .Addr(alu_1_out), .WData(grf_1_rdata2), .Out(datamemory_1_out), .MemWrite(controller_1_memwrite),
    .MemRead(controller_1_memread), .reset(Reset), .Clk(Clk_out));
  Multiplexer #(.select(2), .width(32), .enable("false")) multiplexer_7 (
    .in0(alu_1_out), .in1(datamemory_1_out), .in2({Jimm[15:0], {16{1'b0}}}), .in3(PC_4),
    .out(multiplexer_7_out), .sel(controller_1_resulttoreg));

  // Other names for the same wires on the sheet: Rt[4:0] = Jimm[20:16]; Rs[4:0] = Jimm[25:21]
endmodule

module GRF (
  input  [4:0] ReadReg1,
  input  reset,
  input  [4:0] WriteReg,
  input  Clk,
  input  WriteEn,
  input  [31:0] WData,
  input  [4:0] ReadReg2,
  output [31:0] RData1,
  output [31:0] RData2
);

  wire [7:0] and_1_out_2, and_1_out_3;
  wire [15:0] and_1_out;
  wire [31:0] _0, _1, _2, _3, _4, _5, _6, _7, _8, _9, _10, _11, _12, _13, _14, _15, _16, _17, _18, _19, _20,
       _21, _22, _23, _24, _25, _26, _27, _28, _29, _30, _31, decoder_1_out0, multiplexer_1_out;

  Decoder #(.select(5), .enable("false")) decoder_1 (
    .out0(decoder_1_out0[0]), .out1(decoder_1_out0[1]), .out2(decoder_1_out0[2]), .out3(decoder_1_out0[3]),
    .out4(decoder_1_out0[4]), .out5(decoder_1_out0[5]), .out6(decoder_1_out0[6]), .out7(decoder_1_out0[7]),
    .out8(decoder_1_out0[8]), .out9(decoder_1_out0[9]), .out10(decoder_1_out0[10]),
    .out11(decoder_1_out0[11]), .out12(decoder_1_out0[12]), .out13(decoder_1_out0[13]),
    .out14(decoder_1_out0[14]), .out15(decoder_1_out0[15]), .out16(decoder_1_out0[16]),
    .out17(decoder_1_out0[17]), .out18(decoder_1_out0[18]), .out19(decoder_1_out0[19]),
    .out20(decoder_1_out0[20]), .out21(decoder_1_out0[21]), .out22(decoder_1_out0[22]),
    .out23(decoder_1_out0[23]), .out24(decoder_1_out0[24]), .out25(decoder_1_out0[25]),
    .out26(decoder_1_out0[26]), .out27(decoder_1_out0[27]), .out28(decoder_1_out0[28]),
    .out29(decoder_1_out0[29]), .out30(decoder_1_out0[30]), .out31(decoder_1_out0[31]), .sel(WriteReg));
  Multiplexer #(.width(32), .enable("false")) multiplexer_1 (
    .in0({32{1'b0}}), .in1({32{1'b1}}), .out(multiplexer_1_out), .sel(WriteEn));
  assign {and_1_out_3, and_1_out_2, and_1_out} = decoder_1_out0 & multiplexer_1_out;  // AND_Gate and_1, 32 bits wide
  Register #(.width(32)) u__0 (.D(WData), .en(1'b0), .Q(_0), .clk(Clk), .clr(reset));
  Register #(.width(32)) u__1 (.D(WData), .en(and_1_out[1]), .Q(_1), .clk(Clk), .clr(reset));
  Register #(.width(32)) u__2 (.D(WData), .en(and_1_out[2]), .Q(_2), .clk(Clk), .clr(reset));
  Register #(.width(32)) u__3 (.D(WData), .en(and_1_out[3]), .Q(_3), .clk(Clk), .clr(reset));
  Register #(.width(32)) u__4 (.D(WData), .en(and_1_out[4]), .Q(_4), .clk(Clk), .clr(reset));
  Register #(.width(32)) u__5 (.D(WData), .en(and_1_out[5]), .Q(_5), .clk(Clk), .clr(reset));
  Register #(.width(32)) u__6 (.D(WData), .en(and_1_out[6]), .Q(_6), .clk(Clk), .clr(reset));
  Register #(.width(32)) u__7 (.D(WData), .en(and_1_out[7]), .Q(_7), .clk(Clk), .clr(reset));
  Register #(.width(32)) u__8 (.D(WData), .en(and_1_out[8]), .Q(_8), .clk(Clk), .clr(reset));
  Register #(.width(32)) u__9 (.D(WData), .en(and_1_out[9]), .Q(_9), .clk(Clk), .clr(reset));
  Register #(.width(32)) u__10 (.D(WData), .en(and_1_out[10]), .Q(_10), .clk(Clk), .clr(reset));
  Register #(.width(32)) u__11 (.D(WData), .en(and_1_out[11]), .Q(_11), .clk(Clk), .clr(reset));
  Register #(.width(32)) u__12 (.D(WData), .en(and_1_out[12]), .Q(_12), .clk(Clk), .clr(reset));
  Register #(.width(32)) u__13 (.D(WData), .en(and_1_out[13]), .Q(_13), .clk(Clk), .clr(reset));
  Register #(.width(32)) u__14 (.D(WData), .en(and_1_out[14]), .Q(_14), .clk(Clk), .clr(reset));
  Register #(.width(32)) u__15 (.D(WData), .en(and_1_out[15]), .Q(_15), .clk(Clk), .clr(reset));
  Register #(.width(32)) u__16 (.D(WData), .en(and_1_out_2[0]), .Q(_16), .clk(Clk), .clr(reset));
  Register #(.width(32)) u__17 (.D(WData), .en(and_1_out_2[1]), .Q(_17), .clk(Clk), .clr(reset));
  Register #(.width(32)) u__18 (.D(WData), .en(and_1_out_2[2]), .Q(_18), .clk(Clk), .clr(reset));
  Register #(.width(32)) u__19 (.D(WData), .en(and_1_out_2[3]), .Q(_19), .clk(Clk), .clr(reset));
  Register #(.width(32)) u__20 (.D(WData), .en(and_1_out_2[4]), .Q(_20), .clk(Clk), .clr(reset));
  Register #(.width(32)) u__21 (.D(WData), .en(and_1_out_2[5]), .Q(_21), .clk(Clk), .clr(reset));
  Register #(.width(32)) u__22 (.D(WData), .en(and_1_out_2[6]), .Q(_22), .clk(Clk), .clr(reset));
  Register #(.width(32)) u__23 (.D(WData), .en(and_1_out_2[7]), .Q(_23), .clk(Clk), .clr(reset));
  Register #(.width(32)) u__24 (.D(WData), .en(and_1_out_3[0]), .Q(_24), .clk(Clk), .clr(reset));
  Register #(.width(32)) u__25 (.D(WData), .en(and_1_out_3[1]), .Q(_25), .clk(Clk), .clr(reset));
  Register #(.width(32)) u__26 (.D(WData), .en(and_1_out_3[2]), .Q(_26), .clk(Clk), .clr(reset));
  Register #(.width(32)) u__27 (.D(WData), .en(and_1_out_3[3]), .Q(_27), .clk(Clk), .clr(reset));
  Register #(.width(32)) u__28 (.D(WData), .en(and_1_out_3[4]), .Q(_28), .clk(Clk), .clr(reset));
  Register #(.width(32)) u__29 (.D(WData), .en(and_1_out_3[5]), .Q(_29), .clk(Clk), .clr(reset));
  Register #(.width(32)) u__30 (.D(WData), .en(and_1_out_3[6]), .Q(_30), .clk(Clk), .clr(reset));
  Register #(.width(32)) u__31 (.D(WData), .en(and_1_out_3[7]), .Q(_31), .clk(Clk), .clr(reset));
  Multiplexer #(.select(5), .width(32), .enable("false")) multiplexer_2 (
    .in0(_0), .in1(_1), .in2(_2), .in3(_3), .in4(_4), .in5(_5), .in6(_6), .in7(_7), .in8(_8), .in9(_9),
    .in10(_10), .in11(_11), .in12(_12), .in13(_13), .in14(_14), .in15(_15), .in16(_16), .in17(_17),
    .in18(_18), .in19(_19), .in20(_20), .in21(_21), .in22(_22), .in23(_23), .in24(_24), .in25(_25),
    .in26(_26), .in27(_27), .in28(_28), .in29(_29), .in30(_30), .in31(_31), .out(RData1), .sel(ReadReg1));
  Multiplexer #(.select(5), .width(32), .enable("false")) multiplexer_3 (
    .in0(_0), .in1(_1), .in2(_2), .in3(_3), .in4(_4), .in5(_5), .in6(_6), .in7(_7), .in8(_8), .in9(_9),
    .in10(_10), .in11(_11), .in12(_12), .in13(_13), .in14(_14), .in15(_15), .in16(_16), .in17(_17),
    .in18(_18), .in19(_19), .in20(_20), .in21(_21), .in22(_22), .in23(_23), .in24(_24), .in25(_25),
    .in26(_26), .in27(_27), .in28(_28), .in29(_29), .in30(_30), .in31(_31), .out(RData2), .sel(ReadReg2));
endmodule

module DataMemory (
  input  MemWrite,
  input  MemRead,
  input  [31:0] Addr,
  input  Clk,
  input  reset,
  input  [31:0] WData,
  output [31:0] Out
);

  RAM #(.addrWidth(5), .dataWidth(32), .bus("separate")) ram_1 (
    .addr(Addr[6:2]), .din(WData), .data(Out), .str(MemWrite), .clk(Clk), .ld(MemRead), .clr(reset));  // open: sel
endmodule

module ALU (
  input  [31:0] A,
  input  [31:0] B,
  input  [2:0] ALUOp,
  input  [1:0] CmpSel,
  input  OutSel,
  output [31:0] Out,
  output Zero
);

  wire comparator_1_eq, comparator_1_gt, comparator_1_lt;
  wire [31:0] adder_1_out, and_1_out, multiplexer_1_out, multiplexer_4_out, or_1_out, shifter_1_out,
       shifter_2_out, subtractor_1_out;

  Adder #(.width(32)) adder_1 (.a(A), .b(B), .out(adder_1_out));  // open: cin, cout
  Subtractor #(.width(32)) subtractor_1 (.a(A), .b(B), .out(subtractor_1_out));  // open: bin, bout
  assign or_1_out = A | B;  // OR_Gate or_1, 32 bits wide
  assign and_1_out = A & B;  // AND_Gate and_1, 32 bits wide
  Comparator #(.width(32)) comparator_1 (
    .a(A), .b(B), .gt(comparator_1_gt), .eq(comparator_1_eq), .lt(comparator_1_lt));
  Shifter #(.width(32)) shifter_1 (.in(A), .\dist (B[4:0]), .out(shifter_1_out));
  Shifter #(.width(32), .shift("lr")) shifter_2 (.in(A), .\dist (B[4:0]), .out(shifter_2_out));
  Multiplexer #(.select(3), .width(32), .enable("false")) multiplexer_1 (
    .in0(adder_1_out), .in1(subtractor_1_out), .in2(or_1_out), .in3(and_1_out), .in4(shifter_1_out),
    .in5(shifter_2_out), .out(multiplexer_1_out), .sel(ALUOp));  // open: in6, in7
  Multiplexer #(.width(32), .enable("false")) multiplexer_2 (
    .in0(multiplexer_1_out), .in1(multiplexer_4_out), .out(Out), .sel(OutSel));
  Multiplexer #(.select(2), .enable("false")) multiplexer_3 (
    .in0(comparator_1_eq), .in1(comparator_1_gt), .in2(comparator_1_lt), .out(Zero), .sel(CmpSel));  // open: in3
  Multiplexer #(.width(32), .enable("false")) multiplexer_4 (
    .in0({32{1'b0}}), .in1(32'h1), .out(multiplexer_4_out), .sel(Zero));
endmodule

module Controller (
  input  [5:0] Op,
  input  [5:0] Func,
  output MemRead,
  output MemWrite,
  output WriteEn,
  output [1:0] Jump,
  output Branch,
  output [1:0] WriteRegDist,
  output [1:0] ResultToReg,
  output ALUSrcA,
  output [1:0] ALUSrcB,
  output [2:0] ALUOp,
  output [1:0] CmpSel,
  output OutSel,
  output ExtOp
);

  wire addu, \and , beq, bltz, j, jalr, jr, lui, not_1_out, not_2_out, not_3_out, not_4_out, not_5_out,
       not_6_out, not_7_out, not_8_out, not_9_out, not_10_out, not_11_out, not_12_out, \or , sll, srl, subu;

  not not_1 (not_1_out, Op[5]);
  not not_2 (not_2_out, Op[4]);
  not not_3 (not_3_out, Op[3]);
  not not_4 (not_4_out, Op[2]);
  not not_5 (not_5_out, Op[0]);
  not not_6 (not_6_out, Op[1]);
  not not_7 (not_7_out, Func[4]);
  not not_8 (not_8_out, Func[5]);
  not not_9 (not_9_out, Func[2]);
  not not_10 (not_10_out, Func[3]);
  not not_11 (not_11_out, Func[0]);
  not not_12 (not_12_out, Func[1]);
  and u_addu (addu, Func[5], not_7_out, not_10_out, not_9_out, not_12_out, Func[0], not_5_out, not_6_out, not_4_out, not_3_out, not_2_out, not_1_out);
  and u_subu (subu, Func[5], not_7_out, not_10_out, not_9_out, Func[1], Func[0], not_5_out, not_6_out, not_4_out, not_3_out, not_2_out, not_1_out);
  and u_sll (sll, not_11_out, not_12_out, not_9_out, not_10_out, not_7_out, not_8_out, not_5_out, not_6_out, not_4_out, not_3_out, not_2_out, not_1_out);
  and ori (ExtOp, not_1_out, not_2_out, Op[3], Op[2], not_6_out, Op[0]);
  and lw (MemRead, Op[5], not_2_out, not_3_out, not_4_out, Op[1], Op[0]);
  and sw (MemWrite, Op[5], not_2_out, Op[3], not_4_out, Op[1], Op[0]);
  and u_lui (lui, not_1_out, not_2_out, Op[3], Op[2], Op[1], Op[0]);
  and u_beq (beq, not_1_out, not_2_out, not_3_out, Op[2], not_6_out, not_5_out);
  and u_j (j, not_1_out, not_2_out, not_3_out, not_4_out, Op[1], not_5_out);
  and jal (WriteRegDist[1], not_1_out, not_2_out, not_3_out, not_4_out, Op[1], Op[0]);
  and u_jalr (jalr, not_1_out, not_2_out, not_3_out, not_4_out, not_6_out, not_5_out, not_8_out, not_7_out, Func[3], not_9_out, not_12_out, Func[0]);
  and u_jr (jr, not_1_out, not_2_out, not_3_out, not_4_out, not_6_out, not_5_out, not_8_out, not_7_out, Func[3], not_9_out, not_12_out, not_11_out);
  and slt (OutSel, not_1_out, not_2_out, not_3_out, not_4_out, not_6_out, not_5_out, Func[5], not_7_out, Func[3], not_9_out, Func[1], not_11_out);
  and u_and (\and , not_1_out, not_2_out, not_3_out, not_4_out, not_6_out, not_5_out, Func[5], not_7_out, not_10_out, Func[2], not_12_out, not_11_out);
  and u_srl (srl, not_1_out, not_2_out, not_3_out, not_4_out, not_6_out, not_5_out, not_8_out, not_7_out, not_10_out, not_9_out, Func[1], not_11_out);
  and u_bltz (bltz, not_1_out, not_2_out, not_3_out, not_4_out, not_6_out, Op[0]);
  and bgtz (CmpSel[0], not_1_out, not_2_out, not_3_out, Op[2], Op[1], Op[0]);
  and u_or (\or , not_1_out, not_2_out, not_3_out, not_4_out, not_6_out, not_5_out, Func[5], not_7_out, not_10_out, Func[2], not_12_out, Func[0]);
  or or_2 (WriteRegDist[0], addu, subu, \and , \or , jalr, sll, srl, OutSel);
  or or_3 (ALUSrcB[1], sll, bltz, CmpSel[0], srl);
  or or_4 (Jump[0], j, WriteRegDist[1]);
  or or_5 (Jump[1], jr, jalr);
  or or_6 (Branch, beq, CmpSel[0], bltz);
  or or_7 (ResultToReg[0], MemRead, WriteRegDist[1], jalr);
  or or_8 (ResultToReg[1], WriteRegDist[1], jalr, lui);
  or or_9 (ALUSrcA, sll, srl);
  or or_10 (ALUSrcB[0], MemWrite, MemRead, ExtOp, bltz, CmpSel[0]);
  or or_11 (ALUOp[0], srl, \and , subu);
  or or_12 (ALUOp[1], \or , ExtOp, \and );
  or or_13 (ALUOp[2], sll, srl);
  or or_14 (CmpSel[1], OutSel, bltz);
  or or_15 (WriteEn, addu, subu, ExtOp, lui, MemRead, \or , \and , sll, srl, OutSel, WriteRegDist[1], jalr);

  // Other names for the same wires on the sheet: bgtz = CmpSel[0]; lw = MemRead; ori = ExtOp; slt = OutSel;
  //   sw = MemWrite; jal = WriteRegDist[1]
endmodule

module IFU (
  input  [31:0] PC_Update,
  input  Clk,
  input  Reset,
  output [31:0] PC_current,
  output [31:0] Instruction
);

  Register #(.width(32)) PC (.D(PC_Update), .Q(PC_current), .clk(Clk), .clr(Reset));  // open: en
  ROM #(.addrWidth(5), .dataWidth(32)) rom_1 (.addr(PC_current[6:2]), .data(Instruction));  // open: sel

  // Notes on the sheet:
  //   contents of rom_1 (hex, n*v repeats v):
  //   3c010001 3421f12d 211021 411824 120c0 22942 3c06ffff 34c6ffff 1cc00003 4200002 463821 e44023
endmodule

module main_1 (
  input  Reset,
  output [31:0] out_2,
  output out_3,
  output [4:0] out_4,
  output [31:0] out_5,
  output out_6,
  output [4:0] out_7,
  output [31:0] out_8
);

  wire alu1_1_zero, and_1_out, Clk_out, controller1_1_alusrc, controller1_1_branch, controller1_1_extop,
       controller1_1_memread, controller1_1_writeregdist;
  wire [1:0] controller1_1_aluop, controller1_1_memtoreg;
  wire [31:0] adder_1_out, adder_2_out, alu1_1_outcome, bit_extender_2_out, datamemory_1_out, grf_1_rdata1,
       ifu_1_pc_current, multiplexer_2_out, multiplexer_3_out, multiplexer_4_out, shifter_1_out, sign_ext;

  Clock Clk (.out(Clk_out));
  IFU ifu_1 (
    .PC_Update(multiplexer_2_out), .Reset(Reset), .Instruction(out_2), .PC_current(ifu_1_pc_current),
    .Clk(Clk_out));
  Adder #(.width(32)) adder_1 (.a(32'h4), .b(ifu_1_pc_current), .out(adder_1_out));  // open: cin, cout
  Multiplexer #(.width(5), .enable("false")) multiplexer_1 (
    .in0(out_2[20:16]), .in1(out_2[15:11]), .out(out_4), .sel(controller1_1_writeregdist));
  Shifter #(.width(32)) shifter_1 (.in(sign_ext), .\dist (5'b00010), .out(shifter_1_out));
  Controller1 controller1_1 (
    .Op(out_2[31:26]), .Func(out_2[5:0]), .WriteRegDist(controller1_1_writeregdist),
    .Branch(controller1_1_branch), .MemtoReg(controller1_1_memtoreg), .MemWrite(out_6),
    .MemRead(controller1_1_memread), .ALUOp(controller1_1_aluop), .ALUSrc(controller1_1_alusrc),
    .RegWrite(out_3), .ExtOp(controller1_1_extop));
  and and_1 (and_1_out, controller1_1_branch, alu1_1_zero);
  Adder #(.width(32)) adder_2 (.a(adder_1_out), .b(shifter_1_out), .out(adder_2_out));  // open: cin, cout
  assign sign_ext = {{16{out_2[15]}}, out_2[15:0]};  // Bit_Extender bit_extender_1
  assign bit_extender_2_out = {{16{1'b0}}, out_2[15:0]};  // Bit_Extender bit_extender_2
  Multiplexer #(.width(32), .enable("false")) multiplexer_2 (
    .in0(adder_1_out), .in1(adder_2_out), .out(multiplexer_2_out), .sel(and_1_out));
  GRF grf_1 (
    .ReadReg1(out_2[25:21]), .WriteReg(out_4), .WriteEn(out_3), .WData(out_5), .RData1(grf_1_rdata1),
    .RData2(out_8), .ReadReg2(out_2[20:16]), .reset(Reset), .Clk(Clk_out));
  Multiplexer #(.width(32), .enable("false")) multiplexer_3 (
    .in0(sign_ext), .in1(bit_extender_2_out), .out(multiplexer_3_out), .sel(controller1_1_extop));
  Multiplexer #(.width(32), .enable("false")) multiplexer_4 (
    .in0(out_8), .in1(multiplexer_3_out), .out(multiplexer_4_out), .sel(controller1_1_alusrc));
  ALU1 alu1_1 (
    .A(grf_1_rdata1), .Outcome({alu1_1_outcome[31:7], out_7, alu1_1_outcome[1:0]}), .B(multiplexer_4_out),
    .Zero(alu1_1_zero), .ALUOp(controller1_1_aluop));
  DataMemory datamemory_1 (
    .Addr({alu1_1_outcome[31:7], out_7, alu1_1_outcome[1:0]}), .WData(out_8), .Out(datamemory_1_out),
    .MemWrite(out_6), .MemRead(controller1_1_memread), .reset(Reset), .Clk(Clk_out));
  Multiplexer #(.select(2), .width(32), .enable("false")) multiplexer_5 (
    .in0({alu1_1_outcome[31:7], out_7, alu1_1_outcome[1:0]}), .in1(datamemory_1_out),
    .in2({out_2[15:0], {16{1'b0}}}), .out(out_5), .sel(controller1_1_memtoreg));  // open: in3

  // Other names for the same wires on the sheet: MemAddr[4:0] = out_7; Instr[31:0] = out_2; MemData[31:0] = out_8;
  //   MemWrite = out_6; RegAddr[4:0] = out_4; RegData[31:0] = out_5; RegWrite = out_3
endmodule

module ALU1 (
  input  [31:0] A,
  input  [31:0] B,
  input  [1:0] ALUOp,
  output [31:0] Outcome,
  output Zero
);

  wire [31:0] adder_1_out, or_1_out, subtractor_1_out;

  Adder #(.width(32)) adder_1 (.a(A), .b(B), .out(adder_1_out));  // open: cin, cout
  Subtractor #(.width(32)) subtractor_1 (.a(A), .b(B), .out(subtractor_1_out));  // open: bin, bout
  assign or_1_out = A | B;  // OR_Gate or_1, 32 bits wide
  Comparator #(.width(32), .mode("unsigned")) comparator_1 (.a(A), .b(B), .eq(Zero));  // open: gt, lt
  Multiplexer #(.select(2), .width(32), .enable("false")) multiplexer_1 (
    .in0(adder_1_out), .in1(subtractor_1_out), .in2(or_1_out), .out(Outcome), .sel(ALUOp));  // open: in3
endmodule

module Controller1 (
  input  [5:0] Op,
  input  [5:0] Func,
  output Branch,
  output [1:0] MemtoReg,
  output MemWrite,
  output MemRead,
  output [1:0] ALUOp,
  output ALUSrc,
  output RegWrite,
  output WriteRegDist,
  output ExtOp
);

  wire addu, nop, not_1_out, not_2_out, not_3_out, not_4_out, not_5_out, not_6_out, not_7_out, not_8_out,
       not_9_out, not_10_out, not_11_out, not_12_out;

  not not_1 (not_1_out, Op[5]);
  not not_2 (not_2_out, Op[4]);
  not not_3 (not_3_out, Op[2]);
  not not_4 (not_4_out, Op[3]);
  not not_5 (not_5_out, Op[0]);
  not not_6 (not_6_out, Op[1]);
  not not_7 (not_7_out, Func[4]);
  not not_8 (not_8_out, Func[5]);
  not not_9 (not_9_out, Func[2]);
  not not_10 (not_10_out, Func[3]);
  not not_11 (not_11_out, Func[0]);
  not not_12 (not_12_out, Func[1]);
  and u_addu (addu, Func[5], not_7_out, not_10_out, not_9_out, not_12_out, Func[0], not_5_out, not_6_out, not_3_out, not_4_out, not_2_out, not_1_out);
  and subu (ALUOp[0], Func[5], not_7_out, not_10_out, not_9_out, Func[1], Func[0], not_5_out, not_6_out, not_3_out, not_4_out, not_2_out, not_1_out);
  and u_nop (nop, not_11_out, not_12_out, not_9_out, not_10_out, not_7_out, not_8_out, not_5_out, not_6_out, not_3_out, not_4_out, not_2_out, not_1_out);
  and ori (ALUOp[1], not_1_out, not_2_out, Op[3], Op[2], not_6_out, Op[0]);
  and lw (MemRead, Op[5], not_2_out, not_4_out, not_3_out, Op[1], Op[0]);
  and sw (MemWrite, Op[5], not_2_out, Op[3], not_3_out, Op[1], Op[0]);
  and lui (MemtoReg[1], not_1_out, not_2_out, Op[3], Op[2], Op[1], Op[0]);
  and beq (Branch, not_1_out, not_2_out, not_4_out, Op[2], not_6_out, not_5_out);
  or or_1 (ALUSrc, ALUOp[1], MemRead, MemWrite);
  or or_2 (RegWrite, addu, ALUOp[0], ALUOp[1], MemRead, MemtoReg[1]);
  or or_3 (WriteRegDist, addu, ALUOp[0]);

  assign ExtOp = ALUOp[1];
  assign MemtoReg[0] = MemRead;

  // Other names for the same wires on the sheet: subu = ALUOp[0]; ori = ALUOp[1]; beq = Branch; lw = MemRead;
  //   lui = MemtoReg[1]; sw = MemWrite
endmodule
