// Logisim project PerCycleCPU.circ as structural Verilog: 6 circuits, main circuit main
module main (
  input  Reset,
  output [31:0] out_2,
  output out_3,
  output [4:0] out_4,
  output [31:0] out_5,
  output out_6,
  output [4:0] out_7,
  output [31:0] out_8
);

  wire alu_1_zero, and_1_out, control_unit_1_alusrc, control_unit_1_branch, control_unit_1_memread,
       control_unit_1_writeregdist;
  wire [1:0] control_unit_1_aluop, control_unit_1_memtoreg;
  wire [31:0] adder_1_out, adder_2_out, alu_1_outcome, datamemory_1_out, grf_1_rdata1, ifu_1_pc_current,
       multiplexer_2_out, multiplexer_3_out, shifter_1_out, sign_ext;

  IFU ifu_1 (.PC_Update(multiplexer_2_out), .Reset(Reset), .Instruction(out_2), .PC_current(ifu_1_pc_current));
  Adder #(.width(32)) adder_1 (.a(32'h4), .b(ifu_1_pc_current), .out(adder_1_out));  // open: cin, cout
  Multiplexer #(.width(5), .enable("false")) multiplexer_1 (
    .in0(out_2[20:16]), .in1(out_2[15:11]), .out(out_4), .sel(control_unit_1_writeregdist));
  Shifter #(.width(32)) shifter_1 (.in(sign_ext), .\dist (5'b00010), .out(shifter_1_out));
  Control_Unit control_unit_1 (
    .Op(out_2[31:26]), .Func(out_2[5:0]), .WriteRegDist(control_unit_1_writeregdist),
    .Branch(control_unit_1_branch), .MemtoReg(control_unit_1_memtoreg), .MemWrite(out_6),
    .MemRead(control_unit_1_memread), .ALUOp(control_unit_1_aluop), .ALUSrc(control_unit_1_alusrc),
    .RegWrite(out_3));
  assign sign_ext = {{16{out_2[15]}}, out_2[15:0]};  // Bit_Extender bit_extender_1
  and and_1 (and_1_out, control_unit_1_branch, alu_1_zero);
  Adder #(.width(32)) adder_2 (.a(adder_1_out), .b(shifter_1_out), .out(adder_2_out));  // open: cin, cout
  Multiplexer #(.width(32), .enable("false")) multiplexer_2 (
    .in0(adder_1_out), .in1(adder_2_out), .out(multiplexer_2_out), .sel(and_1_out));
  GRF grf_1 (
    .ReadReg1(out_2[25:21]), .WriteReg(out_4), .WriteEn(out_3), .WData(out_5), .RData1(grf_1_rdata1),
    .RData2(out_8), .ReadReg2(out_2[20:16]), .reset(Reset));
  Multiplexer #(.width(32), .enable("false")) multiplexer_3 (
    .in0(out_8), .in1(sign_ext), .out(multiplexer_3_out), .sel(control_unit_1_alusrc));
  ALU alu_1 (
    .A(grf_1_rdata1), .B(multiplexer_3_out), .ALUOp(control_unit_1_aluop), .Zero(alu_1_zero),
    .Outcome(alu_1_outcome));
  Bit_Extender #(.in_width(32), .out_width(5)) bit_extender_2 (.in(alu_1_outcome), .out(out_7));
  DataMemory datamemory_1 (
    .Addr(alu_1_outcome), .WData(out_8), .Out(datamemory_1_out), .MemWrite(out_6),
    .MemRead(control_unit_1_memread), .reset(Reset));
  Multiplexer #(.select(2), .width(32), .enable("false")) multiplexer_4 (
    .in0(alu_1_outcome), .in1(datamemory_1_out), .in2({out_2[15:0], {16{1'b0}}}), .out(out_5),
    .sel(control_unit_1_memtoreg));  // open: in3

  // Other names for the same wires on the sheet: Instr[31:0] = out_2; MemAddr[4:0] = out_7; MemData[31:0] = out_8;
  //   MemWrite = out_6; RegAddr[4:0] = out_4; RegData[31:0] = out_5; RegWrite = out_3
endmodule

module GRF (
  input  [4:0] ReadReg1,
  input  reset,
  input  [4:0] WriteReg,
  input  WriteEn,
  input  [31:0] WData,
  input  [4:0] ReadReg2,
  output [31:0] RData1,
  output [31:0] RData2
);

  wire Clk_out;
  wire [7:0] and_1_out_2, and_1_out_3;
  wire [15:0] and_1_out;
  wire [31:0] _0, _1, _2, _3, _4, _5, _6, _7, _8, _9, _10, _11, _12, _13, _14, _15, _16, _17, _18, _19, _20,
       _21, _22, _23, _24, _25, _26, _27, _28, _29, _30, _31, decoder_1_out0, multiplexer_1_out,
       multiplexer_2_out;

  Clock Clk (.out(Clk_out));
  Decoder #(.select(5), .enable("false")) decoder_1 (
    .out0(decoder_1_out0[0]), .out1(decoder_1_out0[1]), .out2(decoder_1_out0[2]), .out3(decoder_1_out0[3]),
    .out4(decoder_1_out0[4]), .out5(decoder_1_out0[5]), .out6(decoder_1_out0[6]), .out7(decoder_1_out0[7]),
    .out8(decoder_1_out0[8]), .out9(decoder_1_out0[9]), .out10(decoder_1_out0[10]),
    .out11(decoder_1_out0[11]), .out12(decoder_1_out0[12]), .out13(decoder_1_out0[13]),
    .out14(decoder_1_out0[14]), .out15(decoder_1_out0[15]), .out16(decoder_1_out0[16]),
    .out17(decoder_1_out0[17]), .out18(decoder_1_out0[18]), .out19(decoder_1_out0[19]),
    .out20(decoder_1_out0[20]), .out21(decoder_1_out0[21]), .out22(decoder_1_out0[22]),
    .out23(decoder_1_out0[23]), .out24(decoder_1_out0[24]), .out25(decoder_1_out0[25]),
    .out26(decoder_1_out0[26]), .out27(decoder_1_out0[27]), .out28(decoder_1_out0[28]),
    .out29(decoder_1_out0[29]), .out30(decoder_1_out0[30]), .out31(decoder_1_out0[31]), .sel(WriteReg));
  Multiplexer #(.width(32), .enable("false")) multiplexer_1 (
    .in0({32{1'b0}}), .in1({32{1'b1}}), .out(multiplexer_1_out), .sel(Clk_out));
  Multiplexer #(.width(32), .enable("false")) multiplexer_2 (
    .in0({32{1'b0}}), .in1({32{1'b1}}), .out(multiplexer_2_out), .sel(WriteEn));
  assign {and_1_out_3, and_1_out_2, and_1_out} = decoder_1_out0 & multiplexer_1_out & multiplexer_2_out;  // AND_Gate and_1, 32 bits wide
  Register #(.width(32)) u__0 (.D(WData), .en(1'b0), .Q(_0), .clk(and_1_out[0]), .clr(reset));
  Register #(.width(32)) u__1 (.D(WData), .Q(_1), .clk(and_1_out[1]), .clr(reset));  // open: en
  Register #(.width(32)) u__2 (.D(WData), .Q(_2), .clk(and_1_out[2]), .clr(reset));  // open: en
  Register #(.width(32)) u__3 (.D(WData), .Q(_3), .clk(and_1_out[3]), .clr(reset));  // open: en
  Register #(.width(32)) u__4 (.D(WData), .Q(_4), .clk(and_1_out[4]), .clr(reset));  // open: en
  Register #(.width(32)) u__5 (.D(WData), .Q(_5), .clk(and_1_out[5]), .clr(reset));  // open: en
  Register #(.width(32)) u__6 (.D(WData), .Q(_6), .clk(and_1_out[6]), .clr(reset));  // open: en
  Register #(.width(32)) u__7 (.D(WData), .Q(_7), .clk(and_1_out[7]), .clr(reset));  // open: en
  Register #(.width(32)) u__8 (.D(WData), .Q(_8), .clk(and_1_out[8]), .clr(reset));  // open: en
  Register #(.width(32)) u__9 (.D(WData), .Q(_9), .clk(and_1_out[9]), .clr(reset));  // open: en
  Register #(.width(32)) u__10 (.D(WData), .Q(_10), .clk(and_1_out[10]), .clr(reset));  // open: en
  Register #(.width(32)) u__11 (.D(WData), .Q(_11), .clk(and_1_out[11]), .clr(reset));  // open: en
  Register #(.width(32)) u__12 (.D(WData), .Q(_12), .clk(and_1_out[12]), .clr(reset));  // open: en
  Register #(.width(32)) u__13 (.D(WData), .Q(_13), .clk(and_1_out[13]), .clr(reset));  // open: en
  Register #(.width(32)) u__14 (.D(WData), .Q(_14), .clk(and_1_out[14]), .clr(reset));  // open: en
  Register #(.width(32)) u__15 (.D(WData), .Q(_15), .clk(and_1_out[15]), .clr(reset));  // open: en
  Register #(.width(32)) u__16 (.D(WData), .Q(_16), .clk(and_1_out_2[0]), .clr(reset));  // open: en
  Register #(.width(32)) u__17 (.D(WData), .Q(_17), .clk(and_1_out_2[1]), .clr(reset));  // open: en
  Register #(.width(32)) u__18 (.D(WData), .Q(_18), .clk(and_1_out_2[2]), .clr(reset));  // open: en
  Register #(.width(32)) u__19 (.D(WData), .Q(_19), .clk(and_1_out_2[3]), .clr(reset));  // open: en
  Register #(.width(32)) u__20 (.D(WData), .Q(_20), .clk(and_1_out_2[4]), .clr(reset));  // open: en
  Register #(.width(32)) u__21 (.D(WData), .Q(_21), .clk(and_1_out_2[5]), .clr(reset));  // open: en
  Register #(.width(32)) u__22 (.D(WData), .Q(_22), .clk(and_1_out_2[6]), .clr(reset));  // open: en
  Register #(.width(32)) u__23 (.D(WData), .Q(_23), .clk(and_1_out_2[7]), .clr(reset));  // open: en
  Register #(.width(32)) u__24 (.D(WData), .Q(_24), .clk(and_1_out_3[0]), .clr(reset));  // open: en
  Register #(.width(32)) u__25 (.D(WData), .Q(_25), .clk(and_1_out_3[1]), .clr(reset));  // open: en
  Register #(.width(32)) u__26 (.D(WData), .Q(_26), .clk(and_1_out_3[2]), .clr(reset));  // open: en
  Register #(.width(32)) u__27 (.D(WData), .Q(_27), .clk(and_1_out_3[3]), .clr(reset));  // open: en
  Register #(.width(32)) u__28 (.D(WData), .Q(_28), .clk(and_1_out_3[4]), .clr(reset));  // open: en
  Register #(.width(32)) u__29 (.D(WData), .Q(_29), .clk(and_1_out_3[5]), .clr(reset));  // open: en
  Register #(.width(32)) u__30 (.D(WData), .Q(_30), .clk(and_1_out_3[6]), .clr(reset));  // open: en
  Register #(.width(32)) u__31 (.D(WData), .Q(_31), .clk(and_1_out_3[7]), .clr(reset));  // open: en
  Multiplexer #(.select(5), .width(32), .enable("false")) multiplexer_3 (
    .in0(_0), .in1(_1), .in2(_2), .in3(_3), .in4(_4), .in5(_5), .in6(_6), .in7(_7), .in8(_8), .in9(_9),
    .in10(_10), .in11(_11), .in12(_12), .in13(_13), .in14(_14), .in15(_15), .in16(_16), .in17(_17),
    .in18(_18), .in19(_19), .in20(_20), .in21(_21), .in22(_22), .in23(_23), .in24(_24), .in25(_25),
    .in26(_26), .in27(_27), .in28(_28), .in29(_29), .in30(_30), .in31(_31), .out(RData1), .sel(ReadReg1));
  Multiplexer #(.select(5), .width(32), .enable("false")) multiplexer_4 (
    .in0(_0), .in1(_1), .in2(_2), .in3(_3), .in4(_4), .in5(_5), .in6(_6), .in7(_7), .in8(_8), .in9(_9),
    .in10(_10), .in11(_11), .in12(_12), .in13(_13), .in14(_14), .in15(_15), .in16(_16), .in17(_17),
    .in18(_18), .in19(_19), .in20(_20), .in21(_21), .in22(_22), .in23(_23), .in24(_24), .in25(_25),
    .in26(_26), .in27(_27), .in28(_28), .in29(_29), .in30(_30), .in31(_31), .out(RData2), .sel(ReadReg2));
endmodule

module DataMemory (
  input  MemWrite,
  input  MemRead,
  input  [31:0] Addr,
  input  reset,
  input  [31:0] WData,
  output [31:0] Out
);

  wire Clk_out;
  wire [4:0] bit_extender_1_out;

  Bit_Extender #(.in_width(32), .out_width(5)) bit_extender_1 (.in(Addr), .out(bit_extender_1_out));
  RAM #(.addrWidth(5), .dataWidth(32), .bus("separate")) ram_1 (
    .addr(bit_extender_1_out), .din(WData), .data(Out), .str(MemWrite), .clk(Clk_out), .ld(MemRead),
    .clr(reset));  // open: sel
  Clock Clk (.out(Clk_out));
endmodule

module ALU (
  input  [31:0] A,
  input  [31:0] B,
  input  [1:0] ALUOp,
  output [31:0] Outcome,
  output Zero
);

  wire [31:0] adder_1_out, or_1_out, subtractor_1_out;

  Adder #(.width(32)) adder_1 (.a(A), .b(B), .out(adder_1_out));  // open: cin, cout
  Subtractor #(.width(32)) subtractor_1 (.a(A), .b(B), .out(subtractor_1_out));  // open: bin, bout
  assign or_1_out = A | B;  // OR_Gate or_1, 32 bits wide
  Comparator #(.width(32), .mode("unsigned")) comparator_1 (.a(A), .b(B), .eq(Zero));  // open: gt, lt
  Multiplexer #(.select(2), .width(32), .enable("false")) multiplexer_1 (
    .in0(adder_1_out), .in1(subtractor_1_out), .in2(or_1_out), .out(Outcome), .sel(ALUOp));  // open: in3
endmodule

module Control_Unit (
  input  [5:0] Op,
  input  [5:0] Func,
  output Branch,
  output [1:0] MemtoReg,
  output MemWrite,
  output MemRead,
  output [1:0] ALUOp,
  output ALUSrc,
  output RegWrite,
  output WriteRegDist
);

  wire addu, nop, not_1_out, not_2_out, not_3_out, not_4_out, not_5_out, not_6_out, not_7_out, not_8_out,
       not_9_out, not_10_out, not_11_out, not_12_out;

  not not_1 (not_1_out, Op[4]);
  not not_2 (not_2_out, Op[5]);
  not not_3 (not_3_out, Op[2]);
  not not_4 (not_4_out, Op[3]);
  not not_5 (not_5_out, Op[0]);
  not not_6 (not_6_out, Op[1]);
  not not_7 (not_7_out, Func[5]);
  not not_8 (not_8_out, Func[4]);
  not not_9 (not_9_out, Func[2]);
  not not_10 (not_10_out, Func[3]);
  not not_11 (not_11_out, Func[0]);
  not not_12 (not_12_out, Func[1]);
  and u_addu (addu, Func[5], not_8_out, not_10_out, not_9_out, not_12_out, Func[0], not_5_out, not_6_out, not_3_out, not_4_out, not_1_out, not_2_out);
  and subu (ALUOp[0], Func[5], not_8_out, not_10_out, not_9_out, Func[1], Func[0], not_5_out, not_6_out, not_3_out, not_4_out, not_1_out, not_2_out);
  and u_nop (nop, not_11_out, not_12_out, not_9_out, not_10_out, not_8_out, not_7_out, not_5_out, not_6_out, not_3_out, not_4_out, not_1_out, not_2_out);
  and ori (ALUOp[1], not_2_out, not_1_out, Op[3], Op[2], not_6_out, Op[0]);
  and lw (MemRead, Op[5], not_1_out, not_4_out, not_3_out, Op[1], Op[0]);
  and sw (MemWrite, Op[5], not_1_out, Op[3], not_3_out, Op[1], Op[0]);
  and lui (MemtoReg[1], not_2_out, not_1_out, Op[3], Op[2], Op[1], Op[0]);
  and beq (Branch, not_2_out, not_1_out, not_4_out, Op[2], not_6_out, not_5_out);
  or or_1 (ALUSrc, ALUOp[1], MemRead, MemWrite);
  or or_2 (RegWrite, addu, ALUOp[0], ALUOp[1], MemRead, MemtoReg[1]);
  or or_3 (WriteRegDist, addu, ALUOp[0]);

  assign MemtoReg[0] = MemRead;

  // Other names for the same wires on the sheet: subu = ALUOp[0]; ori = ALUOp[1]; beq = Branch; lw = MemRead;
  //   lui = MemtoReg[1]; sw = MemWrite
endmodule

module IFU (
  input  [31:0] PC_Update,
  input  Reset,
  output [31:0] PC_current,
  output [31:0] Instruction
);

  wire clock_1_out;

  Clock clock_1 (.out(clock_1_out));
  Register #(.width(32)) PC (.D(PC_Update), .Q(PC_current), .clk(clock_1_out), .clr(Reset));  // open: en
  ROM #(.addrWidth(5), .dataWidth(32)) rom_1 (.addr(PC_current[6:2]), .data(Instruction));  // open: sel

  // Notes on the sheet:
  //   contents of rom_1 (hex, n*v repeats v):
  //   0 3c080001 35080001 1084821 1284823 0 0 0 11290000 ac090000 8c0a0000 1000ffff
endmodule
