// Logisim project alu.circ as structural Verilog
module alu (
  input  [3:0] A,
  input  [3:0] B,
  input  [1:0] ALUOp,
  output [3:0] Out
);

  wire [3:0] add_1_s, and_1_out, or_1_out, sub_1_out;

  ADD add_1 (.A(A), .B(B), .S(add_1_s));
  SUB sub_1 (.A(A), .B(B), .Out(sub_1_out));
  AND and_1 (.A(A), .B(B), .Out(and_1_out));
  OR or_1 (.A(A), .B(B), .Out(or_1_out));
  Multiplexer #(.select(2), .width(4), .enable("false")) multiplexer_1 (
    .in0(add_1_s), .in1(sub_1_out), .in2(and_1_out), .in3(or_1_out), .out(Out), .sel(ALUOp));
endmodule

module _2_bit_full_adder (
  input  [1:0] A,
  input  [1:0] B,
  input  Cin,
  output [1:0] S,
  output Cout
);

  wire n1_bit_full_adder_1_cout;

  _1_bit_full_adder u_1_bit_full_adder_1 (.A(A[0]), .B(B[0]), .Cin(Cin), .S(S[0]), .Cout(n1_bit_full_adder_1_cout));
  _1_bit_full_adder u_1_bit_full_adder_2 (.A(A[1]), .B(B[1]), .Cin(n1_bit_full_adder_1_cout), .S(S[1]), .Cout(Cout));
endmodule

module ADD (
  input  [3:0] A,
  input  [3:0] B,
  output [3:0] S
);

  wire n2_bit_full_adder_1_cout;

  _2_bit_full_adder u_2_bit_full_adder_1 (
    .A(A[1:0]), .B(B[1:0]), .Cin(1'b0), .S(S[1:0]), .Cout(n2_bit_full_adder_1_cout));
  _2_bit_full_adder u_2_bit_full_adder_2 (
    .A(A[3:2]), .B(B[3:2]), .Cin(n2_bit_full_adder_1_cout), .S(S[3:2]));  // open: Cout
endmodule

module _1_bit_full_adder (
  input  A,
  input  B,
  input  Cin,
  output S,
  output Cout
);

  wire and_1_out, and_2_out, and_3_out, and_4_out, and_5_out, and_6_out, and_7_out, not_1_out, not_2_out,
       not_3_out, not_4_out, not_5_out, not_6_out;

  not not_1 (not_1_out, A);
  not not_2 (not_2_out, B);
  not not_3 (not_3_out, A);
  not not_4 (not_4_out, Cin);
  not not_5 (not_5_out, B);
  not not_6 (not_6_out, Cin);
  and and_1 (and_1_out, B, Cin);
  and and_2 (and_2_out, A, Cin);
  and and_3 (and_3_out, A, B);
  and and_4 (and_4_out, not_1_out, not_2_out, Cin);
  and and_5 (and_5_out, not_3_out, B, not_4_out);
  and and_6 (and_6_out, A, not_5_out, not_6_out);
  and and_7 (and_7_out, A, B, Cin);
  or or_1 (Cout, and_1_out, and_2_out, and_3_out);
  or or_2 (S, and_4_out, and_5_out, and_6_out, and_7_out);
endmodule

module SUB (
  input  [3:0] A,
  input  [3:0] B,
  output [3:0] Out
);

  wire [3:0] complement_1_b_prime;

  Complement complement_1 (.B(B), .B_prime(complement_1_b_prime));
  ADD add_1 (.A(A), .B(complement_1_b_prime), .S(Out));
endmodule

module Complement (
  input  [3:0] B,
  output [3:0] B_prime
);

  wire and_1_out, and_2_out, and_3_out, and_4_out, and_5_out, and_6_out, and_7_out, and_8_out, and_9_out,
       not_1_out, not_2_out, not_3_out, not_4_out, not_5_out, not_6_out, not_7_out, not_8_out, not_9_out,
       not_10_out, not_11_out, not_12_out;

  not not_1 (not_1_out, B[3]);
  not not_2 (not_2_out, B[3]);
  not not_3 (not_3_out, B[3]);
  not not_4 (not_4_out, B[2]);
  not not_5 (not_5_out, B[1]);
  not not_6 (not_6_out, B[0]);
  not not_7 (not_7_out, B[2]);
  not not_8 (not_8_out, B[2]);
  not not_9 (not_9_out, B[1]);
  not not_10 (not_10_out, B[0]);
  not not_11 (not_11_out, B[1]);
  not not_12 (not_12_out, B[0]);
  and and_1 (and_1_out, not_1_out, B[0]);
  and and_2 (and_2_out, not_2_out, B[1]);
  and and_3 (and_3_out, not_3_out, B[2]);
  and and_4 (and_4_out, B[3], not_4_out, not_5_out, not_6_out);
  and and_5 (and_5_out, not_7_out, B[0]);
  and and_6 (and_6_out, not_8_out, B[1]);
  and and_7 (and_7_out, B[2], not_9_out, not_10_out);
  and and_8 (and_8_out, not_11_out, B[0]);
  and and_9 (and_9_out, B[1], not_12_out);
  or or_1 (B_prime[3], and_1_out, and_2_out, and_3_out, and_4_out);
  or or_2 (B_prime[2], and_5_out, and_6_out, and_7_out);
  or or_3 (B_prime[1], and_8_out, and_9_out);

  assign B_prime[0] = B[0];
endmodule

module AND (
  input  [3:0] A,
  input  [3:0] B,
  output [3:0] Out
);

  and and_1 (Out[0], A[0], B[0]);
  and and_2 (Out[1], A[1], B[1]);
  and and_3 (Out[2], A[2], B[2]);
  and and_4 (Out[3], A[3], B[3]);
endmodule

module OR (
  input  [3:0] A,
  input  [3:0] B,
  output [3:0] Out
);

  or or_1 (Out[0], A[0], B[0]);
  or or_2 (Out[1], A[1], B[1]);
  or or_3 (Out[2], A[2], B[2]);
  or or_4 (Out[3], A[3], B[3]);
endmodule
