// Logisim project code.circ as structural Verilog
module fsm (
  input  Clr,
  input  X,
  input  [31:0] Count,
  output Z
);

  wire clock_1_out, clock_2_out;
  wire [1:0] register_1_q, state_shift_1_d0;
  wire [31:0] adder_1_out, multiplexer_2_out;

  state_shift state_shift_1 (
    .S1(register_1_q[1]), .S0(register_1_q[0]), .T(X), .D1(state_shift_1_d0[1]), .D0(state_shift_1_d0[0]));
  Clock clock_1 (.out(clock_1_out));
  Register #(.width(2)) register_1 (.D(state_shift_1_d0), .Q(register_1_q), .clk(clock_1_out), .clr(Clr));  // open: en
  Multiplexer #(.select(2), .enable("false")) multiplexer_1 (
    .in0(1'b0), .in1(1'b0), .in2(1'b0), .in3(1'b1), .out(Z), .sel(state_shift_1_d0));
  Multiplexer #(.width(32), .enable("false")) multiplexer_2 (
    .in0({32{1'b0}}), .in1(32'h1), .out(multiplexer_2_out), .sel(Z));
  Adder #(.width(32)) adder_1 (.a(multiplexer_2_out), .b(Count), .out(adder_1_out));  // open: cin, cout
  Register #(.width(32)) register_2 (.D(adder_1_out), .Q(Count), .clk(clock_2_out));  // open: en, clr
  Clock clock_2 (.out(clock_2_out));
endmodule

module state_shift (
  input  S1,
  input  S0,
  input  T,
  output D1,
  output D0
);

  wire and_1_out, and_2_out, not_1_out, not_2_out;

  not not_1 (not_1_out, T);
  not not_2 (not_2_out, S0);
  and and_1 (and_1_out, S0, not_1_out);
  and and_2 (and_2_out, S1, not_2_out, T);
  or or_1 (D1, and_1_out, and_2_out);

  assign D0 = T;
endmodule
