// Logisim project comparator.circ as structural Verilog
module comparator (
  input  [3:0] A,
  input  [3:0] B,
  output Out
);

  wire and_1_out, and_2_out, multiplexer_1_out, multiplexer_2_out, multiplexer_3_out,
       n1bit_comparator_bg_1_out, n1bit_comparator_bg_2_out, n1bit_comparator_bg_3_out,
       n1bit_comparator_bg_4_out, T1, T2, T3;

  _1bit_comparator_be u_1bit_comparator_be_1 (.A(A[2]), .B(B[2]), .out_3(T2));
  _1bit_comparator_be u_1bit_comparator_be_2 (.A(A[1]), .B(B[1]), .out_3(T1));
  _1bit_comparator_bg u_1bit_comparator_bg_1 (.A(A[0]), .B(B[0]), .out(n1bit_comparator_bg_1_out));
  _1bit_comparator_bg u_1bit_comparator_bg_2 (.A(A[2]), .B(B[2]), .out(n1bit_comparator_bg_2_out));
  _1bit_comparator_bg u_1bit_comparator_bg_3 (.A(A[3]), .B(B[3]), .out(n1bit_comparator_bg_3_out));
  _1bit_comparator_be u_1bit_comparator_be_3 (.A(A[3]), .B(B[3]), .out_3(T3));
  Multiplexer #(.enable("false")) multiplexer_1 (
    .in0(1'b0), .in1(n1bit_comparator_bg_2_out), .out(multiplexer_1_out), .sel(T3));
  _1bit_comparator_bg u_1bit_comparator_bg_4 (.A(A[1]), .B(B[1]), .out(n1bit_comparator_bg_4_out));
  and and_1 (and_1_out, T1, T2, T3);
  Multiplexer #(.enable("false")) multiplexer_2 (
    .in0(1'b0), .in1(n1bit_comparator_bg_4_out), .out(multiplexer_2_out), .sel(and_2_out));
  and and_2 (and_2_out, T2, T3);
  Multiplexer #(.enable("false")) multiplexer_3 (
    .in0(1'b0), .in1(n1bit_comparator_bg_1_out), .out(multiplexer_3_out), .sel(and_1_out));
  or or_1 (Out, n1bit_comparator_bg_3_out, multiplexer_1_out, multiplexer_2_out, multiplexer_3_out);
endmodule

module _1bit_comparator_bg (
  input  A,
  input  B,
  output out
);

  wire not_1_out;

  and and_1 (out, A, not_1_out);
  not not_1 (not_1_out, B);
endmodule

module _1bit_comparator_be (
  input  A,
  input  B,
  output out_3
);

  wire and_1_out, and_2_out, not_1_out, not_2_out;

  not not_1 (not_1_out, A);
  not not_2 (not_2_out, B);
  and and_1 (and_1_out, A, B);
  and and_2 (and_2_out, not_1_out, not_2_out);
  or or_1 (out_3, and_1_out, and_2_out);
endmodule
