// Logisim project fibo.circ as structural Verilog: 2 circuits, main circuit main
module main (
  input  [2:0] N,
  output [3:0] Nth
);

  wire clock_1_out, clock_2_out, clock_3_out, comparator_1_eq, multiplexer_1_out, register_3_q;
  wire [2:0] adder_1_out, register_1_q;
  wire [3:0] sonfib_1_out_1;

  Adder #(.width(3)) adder_1 (.a(3'b001), .b(register_1_q), .out(adder_1_out));  // open: cin, cout
  SonFib sonfib_1 (.out_1(sonfib_1_out_1));
  Register #(.width(3)) register_1 (.D(adder_1_out), .Q(register_1_q), .clk(clock_1_out));  // open: en, clr
  Clock clock_1 (.out(clock_1_out));
  Comparator #(.width(3)) comparator_1 (.a(N), .b(register_1_q), .eq(comparator_1_eq));  // open: gt, lt
  Register #(.width(4)) register_2 (
    .D(sonfib_1_out_1), .en(multiplexer_1_out), .Q(Nth), .clk(clock_2_out));  // open: clr
  Clock clock_2 (.out(clock_2_out));
  Register #(.width(1)) register_3 (.D(1'b1), .en(comparator_1_eq), .Q(register_3_q), .clk(clock_3_out));  // open: clr
  Clock clock_3 (.out(clock_3_out));
  Multiplexer #(.enable("false")) multiplexer_1 (
    .in0(comparator_1_eq), .in1(1'b0), .out(multiplexer_1_out), .sel(register_3_q));
endmodule

module SonFib (
  output [3:0] out_1
);

  wire clock_1_out, clock_2_out, clock_3_out, register_1_q;
  wire [3:0] adder_1_out, multiplexer_1_out, register_3_q;

  Clock clock_1 (.out(clock_1_out));
  Register #(.width(1)) register_1 (.D(1'b1), .en(1'b1), .Q(register_1_q), .clk(clock_1_out));  // open: clr
  Multiplexer #(.width(4), .enable("false")) multiplexer_1 (
    .in0(4'b0001), .in1(register_3_q), .out(multiplexer_1_out), .sel(register_1_q));
  Adder #(.width(4)) adder_1 (.a(multiplexer_1_out), .b(out_1), .out(adder_1_out));  // open: cin, cout
  Register #(.width(4)) register_2 (.D(adder_1_out), .en(1'b1), .Q(out_1), .clk(clock_2_out));  // open: clr
  Clock clock_2 (.out(clock_2_out));
  Clock clock_3 (.out(clock_3_out));
  Register #(.width(4)) register_3 (.D(out_1), .en(1'b1), .Q(register_3_q), .clk(clock_3_out));  // open: clr
endmodule
