// Logisim project fibo2.circ as structural Verilog: 7 circuits, main circuit main
module main (
  input  [31:0] N,
  output [31:0] Nth
);

  wire clock_1_out, clock_2_out, comparator_1_eq, comparator_2_eq, multiplexer_2_out, register_3_q;
  wire [5:0] adder_1_out, register_1_q;
  wire [31:0] controlmatrixmulti_1_a, multiplexer_1_out, subtractor_1_out;

  Comparator #(.width(32)) comparator_1 (.a({32{1'b0}}), .b(N), .eq(comparator_1_eq));  // open: gt, lt
  Subtractor #(.width(32)) subtractor_1 (.a(N), .b(32'h1), .out(subtractor_1_out));  // open: bin, bout
  Adder #(.width(6)) adder_1 (.a(6'b000001), .b(register_1_q), .out(adder_1_out));  // open: cin, cout
  ControlMatrixMulti controlmatrixmulti_1 (.in_1(subtractor_1_out), .A(controlmatrixmulti_1_a));
  Register #(.width(6)) register_1 (.D(adder_1_out), .Q(register_1_q), .clk(clock_1_out));  // open: en, clr
  Clock clock_1 (.out(clock_1_out));
  Multiplexer #(.width(32), .enable("false")) multiplexer_1 (
    .in0(controlmatrixmulti_1_a), .in1({32{1'b0}}), .out(multiplexer_1_out), .sel(comparator_1_eq));
  Register #(.width(32)) register_2 (
    .D(multiplexer_1_out), .en(multiplexer_2_out), .Q(Nth), .clk(clock_2_out));  // open: clr
  Clock clock_2 (.out(clock_2_out));
  Comparator #(.width(6), .mode("unsigned")) comparator_2 (
    .a(6'b100000), .b(register_1_q), .eq(comparator_2_eq));  // open: gt, lt
  Register #(.width(1)) register_3 (.D(1'b1), .en(comparator_2_eq), .Q(register_3_q), .clk(clock_1_out));  // open: clr
  Multiplexer #(.enable("false")) multiplexer_2 (
    .in0(comparator_2_eq), .in1(1'b0), .out(multiplexer_2_out), .sel(register_3_q));
endmodule

module N_split (
  input  [31:0] N,
  output \当前分离位的值 
);

  wire clock_1_out;
  wire [4:0] adder_1_out, register_1_q, subtractor_1_out;

  Adder #(.width(5)) adder_1 (.a(5'b00001), .b(register_1_q), .out(adder_1_out));  // open: cin, cout
  Clock clock_1 (.out(clock_1_out));
  Multiplexer #(.select(5), .enable("false")) multiplexer_1 (
    .in0(N[0]), .in1(N[1]), .in2(N[2]), .in3(N[3]), .in4(N[4]), .in5(N[5]), .in6(N[6]), .in7(N[7]),
    .in8(N[8]), .in9(N[9]), .in10(N[10]), .in11(N[11]), .in12(N[12]), .in13(N[13]), .in14(N[14]),
    .in15(N[15]), .in16(N[16]), .in17(N[17]), .in18(N[18]), .in19(N[19]), .in20(N[20]), .in21(N[21]),
    .in22(N[22]), .in23(N[23]), .in24(N[24]), .in25(N[25]), .in26(N[26]), .in27(N[27]), .in28(N[28]),
    .in29(N[29]), .in30(N[30]), .in31(N[31]), .out(\当前分离位的值 ), .sel(subtractor_1_out));
  Register #(.width(5)) register_1 (.D(adder_1_out), .Q(register_1_q), .clk(clock_1_out));  // open: en, clr
  Subtractor #(.width(5)) subtractor_1 (.a(register_1_q), .b(5'b00001), .out(subtractor_1_out));  // open: bin, bout
endmodule

module myMemory (
  input  [31:0] update1,
  input  [31:0] update2,
  input  [31:0] update3,
  input  [31:0] update4,
  output [31:0] Out1,
  output [31:0] Out2,
  output [31:0] Out3,
  output [31:0] Out4
);

  wire clock_1_out, register_1_q;
  wire [31:0] multiplexer_1_out, multiplexer_2_out, multiplexer_3_out, multiplexer_4_out;

  Multiplexer #(.width(32), .enable("false")) multiplexer_1 (
    .in0(32'h1), .in1(update3), .out(multiplexer_1_out), .sel(register_1_q));
  Multiplexer #(.width(32), .enable("false")) multiplexer_2 (
    .in0({32{1'b0}}), .in1(update4), .out(multiplexer_2_out), .sel(register_1_q));
  Register #(.width(1)) register_1 (.D(1'b1), .Q(register_1_q), .clk(clock_1_out));  // open: en, clr
  Clock clock_1 (.out(clock_1_out));
  Multiplexer #(.width(32), .enable("false")) multiplexer_3 (
    .in0(32'h1), .in1(update2), .out(multiplexer_3_out), .sel(register_1_q));
  Multiplexer #(.width(32), .enable("false")) multiplexer_4 (
    .in0(32'h1), .in1(update1), .out(multiplexer_4_out), .sel(register_1_q));
  Register #(.width(32)) NUM1 (.D(multiplexer_4_out), .Q(Out1), .clk(clock_1_out));  // open: en, clr
  Register #(.width(32)) NUM2 (.D(multiplexer_3_out), .Q(Out2), .clk(clock_1_out));  // open: en, clr
  Register #(.width(32)) NUM3 (.D(multiplexer_1_out), .Q(Out3), .clk(clock_1_out));  // open: en, clr
  Register #(.width(32)) NUM4 (.D(multiplexer_2_out), .Q(Out4), .clk(clock_1_out));  // open: en, clr
endmodule

module AutoMatrixMulti (
  output [31:0] A,
  output [31:0] B,
  output [31:0] C,
  output [31:0] D
);

  wire [31:0] A_t, B_t, C_t, D_t, multiplier_1_out, multiplier_2_out, multiplier_3_out, multiplier_4_out,
       multiplier_5_out, multiplier_6_out, multiplier_7_out, multiplier_8_out, mymemory_1_out3,
       mymemory_2_out1, mymemory_2_out2, mymemory_2_out3, mymemory_2_out4;

  myMemory mymemory_1 (
    .update1(A_t), .update2(B_t), .update3(C_t), .update4(D_t), .Out1(A), .Out2(B), .Out3(mymemory_1_out3),
    .Out4(D));
  myMemory mymemory_2 (
    .update1(A_t), .update2(B_t), .update3(C_t), .update4(D_t), .Out1(mymemory_2_out1),
    .Out2(mymemory_2_out2), .Out3(mymemory_2_out3), .Out4(mymemory_2_out4));
  Multiplier #(.width(32)) multiplier_1 (.a(A), .b(mymemory_2_out1), .out(multiplier_1_out));  // open: cin, cout
  Multiplier #(.width(32)) multiplier_2 (.a(B), .b(mymemory_2_out3), .out(multiplier_2_out));  // open: cin, cout
  Multiplier #(.width(32)) multiplier_3 (.a(A), .b(mymemory_2_out2), .out(multiplier_3_out));  // open: cin, cout
  Multiplier #(.width(32)) multiplier_4 (.a(B), .b(mymemory_2_out4), .out(multiplier_4_out));  // open: cin, cout
  Multiplier #(.width(32)) multiplier_5 (
    .a(mymemory_2_out1), .b(mymemory_1_out3), .out(multiplier_5_out));  // open: cin, cout
  Multiplier #(.width(32)) multiplier_6 (.a(mymemory_2_out3), .b(D), .out(multiplier_6_out));  // open: cin, cout
  Multiplier #(.width(32)) multiplier_7 (
    .a(mymemory_2_out2), .b(mymemory_1_out3), .out(multiplier_7_out));  // open: cin, cout
  Multiplier #(.width(32)) multiplier_8 (.a(D), .b(mymemory_2_out4), .out(multiplier_8_out));  // open: cin, cout
  // Probe on A_t
  Adder #(.width(32)) adder_1 (.a(multiplier_1_out), .b(multiplier_2_out), .out(A_t));  // open: cin, cout
  // Probe on B_t
  Adder #(.width(32)) adder_2 (.a(multiplier_3_out), .b(multiplier_4_out), .out(B_t));  // open: cin, cout
  // Probe on C_t
  Adder #(.width(32)) adder_3 (.a(multiplier_5_out), .b(multiplier_6_out), .out(C_t));  // open: cin, cout
  // Probe on D_t
  Adder #(.width(32)) adder_4 (.a(multiplier_7_out), .b(multiplier_8_out), .out(D_t));  // open: cin, cout

  assign C = B;

  // Other names for the same wires on the sheet: num1[31:0] = A; num2[31:0] = B; num3[31:0] = B; num4[31:0] = D

  // Notes on the sheet:
  //   a1a2
  //   b1c2
  //   a1b2
  //   b1d2
  //   a2c1
  //   c2d1
  //   b2c1
  //   d1d2
endmodule

module ControlMatrixMulti (
  input  [31:0] in_1,
  output [31:0] A
);

  wire [31:0] B, C, D, multichoose_1_a, multichoose_1_b, multichoose_1_c, multichoose_1_d, multiplier_1_out,
       multiplier_2_out, multiplier_3_out, multiplier_4_out, multiplier_5_out, multiplier_6_out,
       multiplier_7_out, multiplier_8_out, mymemory2_1_out1, mymemory2_1_out2, mymemory2_1_out3,
       mymemory2_1_out4;

  MultiChoose multichoose_1 (
    .in_1(in_1), .A(multichoose_1_a), .B(multichoose_1_b), .C(multichoose_1_c), .D(multichoose_1_d));
  myMemory2 mymemory2_1 (
    .update1(A), .update2(B), .update3(C), .update4(D), .Out1(mymemory2_1_out1), .Out2(mymemory2_1_out2),
    .Out3(mymemory2_1_out3), .Out4(mymemory2_1_out4));
  Multiplier #(.width(32)) multiplier_1 (
    .a(multichoose_1_a), .b(mymemory2_1_out1), .out(multiplier_1_out));  // open: cin, cout
  Multiplier #(.width(32)) multiplier_2 (
    .a(multichoose_1_b), .b(mymemory2_1_out3), .out(multiplier_2_out));  // open: cin, cout
  Multiplier #(.width(32)) multiplier_3 (
    .a(multichoose_1_a), .b(mymemory2_1_out2), .out(multiplier_3_out));  // open: cin, cout
  Multiplier #(.width(32)) multiplier_4 (
    .a(multichoose_1_b), .b(mymemory2_1_out4), .out(multiplier_4_out));  // open: cin, cout
  Multiplier #(.width(32)) multiplier_5 (
    .a(multichoose_1_c), .b(mymemory2_1_out1), .out(multiplier_5_out));  // open: cin, cout
  Multiplier #(.width(32)) multiplier_6 (
    .a(multichoose_1_d), .b(mymemory2_1_out3), .out(multiplier_6_out));  // open: cin, cout
  Multiplier #(.width(32)) multiplier_7 (
    .a(multichoose_1_c), .b(mymemory2_1_out2), .out(multiplier_7_out));  // open: cin, cout
  Multiplier #(.width(32)) multiplier_8 (
    .a(multichoose_1_d), .b(mymemory2_1_out4), .out(multiplier_8_out));  // open: cin, cout
  Adder #(.width(32)) adder_1 (.a(multiplier_1_out), .b(multiplier_2_out), .out(A));  // open: cin, cout
  Adder #(.width(32)) adder_2 (.a(multiplier_3_out), .b(multiplier_4_out), .out(B));  // open: cin, cout
  Adder #(.width(32)) adder_3 (.a(multiplier_5_out), .b(multiplier_6_out), .out(C));  // open: cin, cout
  Adder #(.width(32)) adder_4 (.a(multiplier_7_out), .b(multiplier_8_out), .out(D));  // open: cin, cout
endmodule

module myMemory2 (
  input  [31:0] update1,
  input  [31:0] update2,
  input  [31:0] update3,
  input  [31:0] update4,
  output [31:0] Out1,
  output [31:0] Out2,
  output [31:0] Out3,
  output [31:0] Out4
);

  wire clock_1_out, register_1_q;
  wire [31:0] multiplexer_1_out, multiplexer_2_out, multiplexer_3_out, multiplexer_4_out;

  Multiplexer #(.width(32), .enable("false")) multiplexer_1 (
    .in0({32{1'b0}}), .in1(update3), .out(multiplexer_1_out), .sel(register_1_q));
  Multiplexer #(.width(32), .enable("false")) multiplexer_2 (
    .in0(32'h1), .in1(update4), .out(multiplexer_2_out), .sel(register_1_q));
  Register #(.width(1)) register_1 (.D(1'b1), .Q(register_1_q), .clk(clock_1_out));  // open: en, clr
  Clock clock_1 (.out(clock_1_out));
  Multiplexer #(.width(32), .enable("false")) multiplexer_3 (
    .in0({32{1'b0}}), .in1(update2), .out(multiplexer_3_out), .sel(register_1_q));
  Multiplexer #(.width(32), .enable("false")) multiplexer_4 (
    .in0(32'h1), .in1(update1), .out(multiplexer_4_out), .sel(register_1_q));
  Register #(.width(32)) NUM1 (.D(multiplexer_4_out), .Q(Out1), .clk(clock_1_out));  // open: en, clr
  Register #(.width(32)) NUM2 (.D(multiplexer_3_out), .Q(Out2), .clk(clock_1_out));  // open: en, clr
  Register #(.width(32)) NUM3 (.D(multiplexer_1_out), .Q(Out3), .clk(clock_1_out));  // open: en, clr
  Register #(.width(32)) NUM4 (.D(multiplexer_2_out), .Q(Out4), .clk(clock_1_out));  // open: en, clr
endmodule

module MultiChoose (
  input  [31:0] in_1,
  output [31:0] A,
  output [31:0] B,
  output [31:0] C,
  output [31:0] D
);

  wire \n_split_1_当前分离位的值 ;
  wire [31:0] automatrixmulti_1_a, automatrixmulti_1_b, automatrixmulti_1_c, automatrixmulti_1_d;

  // Probe on automatrixmulti_1_a
  // Probe on automatrixmulti_1_b
  AutoMatrixMulti automatrixmulti_1 (
    .A(automatrixmulti_1_a), .B(automatrixmulti_1_b), .C(automatrixmulti_1_c), .D(automatrixmulti_1_d));
  // Probe on automatrixmulti_1_c
  // Probe on automatrixmulti_1_d
  N_split n_split_1 (.N(in_1), .\当前分离位的值 (\n_split_1_当前分离位的值 ));
  Multiplexer #(.width(32), .enable("false")) multiplexer_1 (
    .in0(32'h1), .in1(automatrixmulti_1_a), .out(A), .sel(\n_split_1_当前分离位的值 ));
  Multiplexer #(.width(32), .enable("false")) multiplexer_2 (
    .in0({32{1'b0}}), .in1(automatrixmulti_1_b), .out(B), .sel(\n_split_1_当前分离位的值 ));
  Multiplexer #(.width(32), .enable("false")) multiplexer_3 (
    .in0({32{1'b0}}), .in1(automatrixmulti_1_c), .out(C), .sel(\n_split_1_当前分离位的值 ));
  Multiplexer #(.width(32), .enable("false")) multiplexer_4 (
    .in0(32'h1), .in1(automatrixmulti_1_d), .out(D), .sel(\n_split_1_当前分离位的值 ));
endmodule
