// Logisim project mod7.circ as structural Verilog
module NEXT (
  input  B2,
  input  B1,
  input  B0,
  input  A,
  output C2,
  output C1,
  output C0
);

  wire and_1_out, and_2_out, and_3_out, and_4_out, and_5_out, and_6_out, and_7_out, and_8_out, and_9_out,
       not_1_out, not_2_out, not_3_out, not_4_out, not_5_out, not_6_out, not_7_out, not_8_out, not_9_out,
       not_10_out, not_11_out;

  and and_1 (and_1_out, B1, not_1_out);
  not not_1 (not_1_out, B0);
  and and_2 (and_2_out, B1, not_2_out);
  not not_2 (not_2_out, A);
  and and_3 (and_3_out, B2, B0, A);
  not not_3 (not_3_out, B2);
  and and_4 (and_4_out, not_3_out, not_4_out, B0);
  not not_4 (not_4_out, B1);
  and and_5 (and_5_out, B0, not_5_out);
  not not_5 (not_5_out, A);
  and and_6 (and_6_out, B2, not_6_out, A);
  not not_6 (not_6_out, B0);
  not not_7 (not_7_out, B2);
  not not_8 (not_8_out, B1);
  and and_7 (and_7_out, not_7_out, not_8_out, A);
  not not_9 (not_9_out, B2);
  not not_10 (not_10_out, B0);
  and and_8 (and_8_out, not_9_out, not_10_out, A);
  and and_9 (and_9_out, B2, not_11_out);
  not not_11 (not_11_out, A);
  or or_1 (C2, and_1_out, and_2_out, and_3_out);
  or or_2 (C1, and_4_out, and_5_out, and_6_out);
  or or_3 (C0, and_7_out, and_8_out, and_9_out);
endmodule

module mod7 (
  input  In,
  output S0,
  output S1,
  output S2,
  output S3,
  output S4,
  output S5,
  output S6
);

  wire clock_1_out;
  wire [2:0] next_1_c0, next_2_c0, register_1_q;

  NEXT next_1 (
    .B2(register_1_q[2]), .B1(register_1_q[1]), .B0(register_1_q[0]), .A(In), .C2(next_1_c0[2]),
    .C1(next_1_c0[1]), .C0(next_1_c0[0]));
  Register #(.width(3)) register_1 (.D(next_1_c0), .Q(register_1_q), .clk(clock_1_out));  // open: en, clr
  Clock clock_1 (.out(clock_1_out));
  NEXT next_2 (
    .B2(register_1_q[2]), .B1(register_1_q[1]), .B0(register_1_q[0]), .A(In), .C2(next_2_c0[2]),
    .C1(next_2_c0[1]), .C0(next_2_c0[0]));
  Decoder #(.select(3)) decoder_1 (
    .out0(S0), .out1(S1), .out2(S2), .out3(S3), .out4(S4), .out5(S5), .out6(S6), .sel(next_2_c0));  // open: out7, en
endmodule
