// Logisim project 单周期.circ as structural Verilog
module Add (
  input  [31:0] PC,
  input  [31:0] Add_Out,
  input  [31:0] CONST
);

  wire [31:0] adder_1_out;

  Adder #(.width(32)) adder_1 (.a(PC), .b(CONST), .out(adder_1_out));  // open: cin, cout
endmodule

module Registers (
  input  [4:0] ReadReg1,
  input  [4:0] WriteReg,
  input  Clk,
  input  [31:0] WriteData,
  input  [4:0] ReadReg2,
  output [31:0] RData1,
  output [31:0] RData2
);

  wire [31:0] _0, _1, _2, _3, _4, _5, _6, _7, _8, _9, _10, _11, _12, _13, _14, _15, _16, _17, _18, _19, _20,
       _21, _22, _23, _24, _25, _26, _27, _28, _29, _30, _31;

  Decoder #(.select(5), .enable("false")) decoder_1 (.sel(WriteReg));  // open: out0, out1, out2, out3, out4, out5, out6, out7, out8, out9, out10, out11, out12, out13, out14, out15, out16, out17, out18, out19, out20, out21, out22, out23, out24, out25, out26, out27, out28, out29, out30, out31
  Register #(.width(32)) u__0 (.en(1'b0), .Q(_0));  // open: D, clk, clr
  Register #(.width(32)) u__1 (.Q(_1));  // open: D, en, clk, clr
  Register #(.width(32)) u__2 (.Q(_2));  // open: D, en, clk, clr
  Register #(.width(32)) u__3 (.Q(_3));  // open: D, en, clk, clr
  Register #(.width(32)) u__4 (.Q(_4));  // open: D, en, clk, clr
  Register #(.width(32)) u__5 (.Q(_5));  // open: D, en, clk, clr
  Register #(.width(32)) u__6 (.Q(_6));  // open: D, en, clk, clr
  Register #(.width(32)) u__7 (.Q(_7));  // open: D, en, clk, clr
  Register #(.width(32)) u__8 (.Q(_8));  // open: D, en, clk, clr
  Register #(.width(32)) u__9 (.Q(_9));  // open: D, en, clk, clr
  Register #(.width(32)) u__10 (.Q(_10));  // open: D, en, clk, clr
  Register #(.width(32)) u__11 (.Q(_11));  // open: D, en, clk, clr
  Register #(.width(32)) u__12 (.Q(_12));  // open: D, en, clk, clr
  Register #(.width(32)) u__13 (.Q(_13));  // open: D, en, clk, clr
  Register #(.width(32)) u__14 (.Q(_14));  // open: D, en, clk, clr
  Register #(.width(32)) u__15 (.Q(_15));  // open: D, en, clk, clr
  Register #(.width(32)) u__16 (.Q(_16));  // open: D, en, clk, clr
  Register #(.width(32)) u__17 (.Q(_17));  // open: D, en, clk, clr
  Register #(.width(32)) u__18 (.Q(_18));  // open: D, en, clk, clr
  Register #(.width(32)) u__19 (.Q(_19));  // open: D, en, clk, clr
  Register #(.width(32)) u__20 (.Q(_20));  // open: D, en, clk, clr
  Register #(.width(32)) u__21 (.Q(_21));  // open: D, en, clk, clr
  Register #(.width(32)) u__22 (.Q(_22));  // open: D, en, clk, clr
  Register #(.width(32)) u__23 (.Q(_23));  // open: D, en, clk, clr
  Register #(.width(32)) u__24 (.Q(_24));  // open: D, en, clk, clr
  Register #(.width(32)) u__25 (.Q(_25));  // open: D, en, clk, clr
  Register #(.width(32)) u__26 (.Q(_26));  // open: D, en, clk, clr
  Register #(.width(32)) u__27 (.Q(_27));  // open: D, en, clk, clr
  Register #(.width(32)) u__28 (.Q(_28));  // open: D, en, clk, clr
  Register #(.width(32)) u__29 (.Q(_29));  // open: D, en, clk, clr
  Register #(.width(32)) u__30 (.Q(_30));  // open: D, en, clk, clr
  Register #(.width(32)) u__31 (.Q(_31));  // open: D, en, clk, clr
  Multiplexer #(.select(5), .width(32), .enable("false")) multiplexer_1 (
    .in0(_0), .in1(_1), .in2(_2), .in3(_3), .in4(_4), .in5(_5), .in6(_6), .in7(_7), .in8(_8), .in9(_9),
    .in10(_10), .in11(_11), .in12(_12), .in13(_13), .in14(_14), .in15(_15), .in16(_16), .in17(_17),
    .in18(_18), .in19(_19), .in20(_20), .in21(_21), .in22(_22), .in23(_23), .in24(_24), .in25(_25),
    .in26(_26), .in27(_27), .in28(_28), .in29(_29), .in30(_30), .in31(_31), .out(RData1), .sel(ReadReg1));
  Multiplexer #(.select(5), .width(32), .enable("false")) multiplexer_2 (
    .in0(_0), .in1(_1), .in2(_2), .in3(_3), .in4(_4), .in5(_5), .in6(_6), .in7(_7), .in8(_8), .in9(_9),
    .in10(_10), .in11(_11), .in12(_12), .in13(_13), .in14(_14), .in15(_15), .in16(_16), .in17(_17),
    .in18(_18), .in19(_19), .in20(_20), .in21(_21), .in22(_22), .in23(_23), .in24(_24), .in25(_25),
    .in26(_26), .in27(_27), .in28(_28), .in29(_29), .in30(_30), .in31(_31), .out(RData2), .sel(ReadReg2));
endmodule
